// Digital circuit 4bit_CPU.dig as structural Verilog
module _4bit_CPU (
  input  clk
);

  wire and_1_out, branch, load, noop, not_1_out, or_1_out, pcen, store, wen, zflag;
  wire [0:0] register_1_q;
  wire [1:0] and_2_out, rom_1_d;
  wire [2:0] CU_out;
  wire [3:0] A_q, alu_1_p4, B_q, driver_1_out, driverinvsel_1_out, IR_q, multiplexer_1_out, pc_1_pc, RAM_d;

  and and_1 (and_1_out, branch, zflag);
  or or_1 (or_1_out, pcen, and_1_out);
  PC pc_1 (.Addr(driverinvsel_1_out), .Inc(rom_1_d[0]), .Load(or_1_out), .Clk(clk), .PC(pc_1_pc));
  and and_2 (and_2_out[1], ~register_1_q[0], ~and_2_out[0]);  // And
  assign driverinvsel_1_out = ~pcen ? pc_1_pc : 4'bz;  // DriverInvSel driverinvsel_1
  Register #(.Bits(2)) register_1 (.D(and_2_out), .C(clk), .en(1'b1), .Q({and_2_out[0], register_1_q[0]}));
  RAMDualPort #(.AddrBits(4), .isProgramMemory("true"), .Bits(4)) RAM (
    .A(driverinvsel_1_out), .Din(driver_1_out), .str(store), .C(clk), .ld(1'b1), .D(RAM_d));
  ROM #(.Bits(2)) rom_1 (.A({and_2_out[0], register_1_q[0]}), .sel(1'b1), .D(rom_1_d));
  Register #(.Bits(4)) IR (.D(RAM_d), .C(clk), .en(rom_1_d[1]), .Q(IR_q));
  LookUpTable #(.Bits(9)) CU (
    .in0(IR_q[0]), .in1(IR_q[1]), .in2(IR_q[2]), .in3(IR_q[3]),
    .out({noop, pcen, branch, store, load, wen, CU_out}));
  Register #(.Bits(4)) A (.D(RAM_d), .C(clk), .en(wen), .Q(A_q));
  Register #(.Bits(4)) B (.D(RAM_d), .C(clk), .en(wen), .Q(B_q));
  // ALU alu_1: pin names not known; wires that end beside it: A_q, B_q, CU_out, alu_1_p4, zflag
  Multiplexer #(.Bits(4)) multiplexer_1 (.sel(not_1_out), .in_0(A_q), .in_1(alu_1_p4), .out(multiplexer_1_out));
  not not_1 (not_1_out, noop);
  assign driver_1_out = store ? multiplexer_1_out : 4'bz;  // Driver driver_1
  assign driverinvsel_1_out = pcen ? multiplexer_1_out : 4'bz;  // Driver driver_2

  // Notes on the sheet:
  //   contents of rom_1 (hex, n*v repeats v):
  //   3
  //   contents of CU (hex, n*v repeats v):
  //   0,18,38,90,30,150,151,152,153,154,155
endmodule
