// Digital circuit PC.dig as structural Verilog
module PC (
  input  [3:0] Addr,
  input  Inc,
  input  Load,
  input  Clk,
  output [3:0] PC
);

  wire or_1_out;
  wire [3:0] multiplexer_1_out, PC_plus_1_p1;

  or or_1 (or_1_out, Inc, Load);
  Multiplexer #(.Bits(4)) multiplexer_1 (.sel(Load), .in_0(PC_plus_1_p1), .in_1(Addr), .out(multiplexer_1_out));
  Register #(.Bits(4)) register_1 (.D(multiplexer_1_out), .C(Clk), .en(or_1_out), .Q(PC));
  // _4bit_full_adder PC_plus_1: pin names not known; wires that end beside it: PC_plus_1_p1, 1'b1, 4'b0000, PC
endmodule
