// Digital circuit cpu.dig as structural Verilog
module cpu (
);

  wire A_q, B_q;
  wire [3:0] pc_1_p1, RAM_d;

  // PC pc_1: pin names not known; wires that end beside it: pc_1_p1
  RAMDualPort #(.AddrBits(4), .Bits(4)) RAM (.A(pc_1_p1), .D(RAM_d));  // open: Din, str, C, ld
  Register #(.Bits(4)) IR (.D(RAM_d));  // open: C, en, Q
  Register A (.Q(A_q));  // open: D, C, en
  Register B (.Q(B_q));  // open: D, C, en
  // ALU ALU: pin names not known; wires that end beside it: A_q, B_q
endmodule
