// Digital circuit register_file.dig as structural Verilog
module register_file (
  input  wdata,
  input  rd,
  input  wen,
  input  rs1,
  input  rs2,
  output [3:0] rdata1,
  output [3:0] rdata2
);

  wire clk;
  wire [3:0] A_q, B_q, demultiplexer_1_out_0, demultiplexer_1_out_1;

  Demultiplexer demultiplexer_1 (
    .sel(rd), .in(wdata), .out_0(demultiplexer_1_out_0[0]), .out_1(demultiplexer_1_out_1[0]));
  Register #(.Bits(4)) A (.D(demultiplexer_1_out_0), .C(clk), .en(wen), .Q(A_q));
  Register #(.Bits(4)) B (.D(demultiplexer_1_out_1), .C(clk), .en(wen), .Q(B_q));
  Multiplexer #(.Bits(4)) multiplexer_1 (.sel(rs1), .in_0(A_q), .in_1(B_q), .out(rdata1));
  Multiplexer #(.Bits(4)) multiplexer_2 (.sel(rs2), .in_0(A_q), .in_1(B_q), .out(rdata2));
  // Pins of 1 and 4 bits meet at demultiplexer_1_out_0
  // Pins of 1 and 4 bits meet at demultiplexer_1_out_1
  // Pins of 1 and 4 bits meet at rdata1
  // Pins of 1 and 4 bits meet at rdata2
endmodule
